# Fritzing sketch REOJ GIRATORIO POV (saved by Fritzing 0.9.3b)
circuit board: 19.9903cm x 4.09068cm
breadboards: 1

parts:
  LED1 = LED - 5mm [color="Red (633nm)" package="5 mm [THT]"]
  LED2 = LED - 5mm [color="Red (633nm)" package="5 mm [THT]"]
  LED3 = LED - 5mm [color="Red (633nm)" package="5 mm [THT]"]
  LED4 = LED - 5mm [color="Red (633nm)" package="5 mm [THT]"]
  LED5 = LED - 5mm [color="Red (633nm)" package="5 mm [THT]"]
  LED6 = LED - 5mm [color="Red (633nm)" package="5 mm [THT]"]
  LED7 = LED - 5mm [color="Red (633nm)" package="5 mm [THT]"]
  LED8 = LED - 5mm [color="Red (633nm)" package="5 mm [THT]"]
  LED9 = LED - 5mm [color="Red (633nm)" package="5 mm [THT]"]
  LED10 = LED - 5mm [color="Red (633nm)" package="5 mm [THT]"]
  R2 = Resistor [tolerance=±5% resistance=1k package=THT]
  R1 = Resistor [tolerance=±5% resistance=1k package=THT]
  R3 = Resistor [tolerance=±5% resistance=1k package=THT]
  R4 = Resistor [tolerance=±5% resistance=1k package=THT]
  R5 = Resistor [tolerance=±5% resistance=1k package=THT]
  R6 = Resistor [tolerance=±5% resistance=1k package=THT]
  R7 = Resistor [tolerance=±5% resistance=1k package=THT]
  R8 = Resistor [tolerance=±5% resistance=1k package=THT]
  R9 = Resistor [tolerance=±5% resistance=1k package=THT]
  R10 = Resistor [tolerance=±5% resistance=1k package=THT]
  Componente1 = Arduino Nano (Rev3.0)
  S1 = SWITCH-MOMENTARY-2 [package=reed_switch_plastic]
  R11 = Resistor [tolerance=±5% resistance=220 package=THT]
  U1 = LIPO-110mAh [package=lipo-110]
  Componente2 = DeadOn RTC - DS3234 Breakout

nets:
  GND: LED1.cathode, LED2.cathode, LED3.cathode, LED4.cathode, LED5.cathode, LED6.cathode, LED7.cathode, LED8.cathode, LED9.cathode, LED10.cathode, Componente1.GND, U1.-, Componente2.GND
  N1: LED1.anode, R1.Pin_0
  N2: LED2.anode, R2.Pin_0
  N3: LED3.anode, R3.Pin_0
  N4: LED4.anode, R4.Pin_0
  N5: LED5.anode, R5.Pin_0
  N6: LED6.anode, R6.Pin_0
  N7: LED7.anode, R7.Pin_0
  N8: LED8.anode, R8.Pin_0
  N9: LED9.anode, R9.Pin_0
  N10: LED10.anode, R10.Pin_0
  N11: R2.Pin_1, Componente1.D3
  N12: R1.Pin_1, Componente1.D2
  N13: R3.Pin_1, Componente1.D4
  N14: R4.Pin_1, Componente1.D5
  N15: R5.Pin_1, Componente1.D6
  N16: R6.Pin_1, Componente1.D7
  N17: R7.Pin_1, Componente1.D8
  N18: R8.Pin_1, Componente1.D9
  N19: R9.Pin_1, Componente1.D10
  N20: R10.Pin_1, Componente1.D11/MOSI
  N21: Componente1.VIN, U1.+
  5V: Componente1.5V, S1.1, Componente2.VCC
  N22: Componente1.A7, Componente2.INT/SQW
  N23: Componente1.A5, Componente2.SCLK
  N24: Componente1.D13/SCK, R11.Pin_1
  N25: S1.2, R11.Pin_0
