# Fritzing sketch reloj (saved by Fritzing 0.9.3b)
circuit board: 16.9284cm x 14.3763cm
breadboards: 1

parts:
  Componente1 = Arduino Uno (Rev3)
  LED1 = LED - 5mm [color="Red (633nm)" package="5 mm [THT]"]
  LED2 = LED - 5mm [color="Red (633nm)" package="5 mm [THT]"]
  LED3 = LED - 5mm [color="Red (633nm)" package="5 mm [THT]"]
  LED4 = LED - 5mm [color="Red (633nm)" package="5 mm [THT]"]
  LED5 = LED - 5mm [color="Red (633nm)" package="5 mm [THT]"]
  LED6 = LED - 5mm [color="Red (633nm)" package="5 mm [THT]"]
  LED7 = LED - 5mm [color="Red (633nm)" package="5 mm [THT]"]
  LED8 = LED - 5mm [color="Red (633nm)" package="5 mm [THT]"]
  LED9 = LED - 5mm [color="Red (633nm)" package="5 mm [THT]"]
  LED10 = LED - 5mm [color="Red (633nm)" package="5 mm [THT]"]
  LED11 = LED - 5mm [color="Red (633nm)" package="5 mm [THT]"]
  LED12 = LED - 5mm [color="Red (633nm)" package="5 mm [THT]"]
  LED13 = LED - 5mm [color="Red (633nm)" package="5 mm [THT]"]
  LED14 = LED - 5mm [color="Red (633nm)" package="5 mm [THT]"]
  LED15 = LED - 5mm [color="Red (633nm)" package="5 mm [THT]"]
  LED16 = LED - 5mm [color="Red (633nm)" package="5 mm [THT]"]
  LED17 = LED - 5mm [color="Red (633nm)" package="5 mm [THT]"]
  R1 = Resistor [tolerance=±5% resistance=1k package=THT]
  R2 = Resistor [tolerance=±5% resistance=1k package=THT]
  R3 = Resistor [tolerance=±5% resistance=1k package=THT]
  R4 = Resistor [tolerance=±5% resistance=1k package=THT]
  R5 = Resistor [tolerance=±5% resistance=1k package=THT]
  R6 = Resistor [tolerance=±5% resistance=1k package=THT]
  R7 = Resistor [tolerance=±5% resistance=1k package=THT]
  R8 = Resistor [tolerance=±5% resistance=1k package=THT]
  R9 = Resistor [tolerance=±5% resistance=1k package=THT]
  R10 = Resistor [tolerance=±5% resistance=1k package=THT]
  R11 = Resistor [tolerance=±5% resistance=1k package=THT]
  R12 = Resistor [tolerance=±5% resistance=1k package=THT]
  R13 = Resistor [tolerance=±5% resistance=1k package=THT]
  R14 = Resistor [tolerance=±5% resistance=1k package=THT]
  R15 = Resistor [tolerance=±5% resistance=1k package=THT]
  R16 = Resistor [tolerance=±5% resistance=1k package=THT]
  R17 = Resistor [tolerance=±5% resistance=1k package=THT]
  Componente4 = DeadOn RTC - DS3234 Breakout

nets:
  N1: Componente1.A0, LED14.anode, R16.Pin_0, R16.Pin_1
  N2: Componente1.A1, LED15.anode, R15.Pin_0, R15.Pin_1
  N3: Componente1.A2, LED16.anode, R14.Pin_0, R14.Pin_1
  N4: Componente1.A3, LED17.anode, R13.Pin_0, R13.Pin_1
  N5: Componente1.A4/SDA, Componente4.INT/SQW
  N6: Componente1.A5/SCL, Componente4.SCLK
  N7: Componente1.D8, LED7.anode, R7.Pin_0, R7.Pin_1
  N8: Componente1.D9_PWM, LED8.anode, R8.Pin_0, R8.Pin_1
  N9: Componente1.D10_PWM/SS, LED9.anode, R9.Pin_0, R9.Pin_1
  N10: Componente1.D11_PWM/MOSI, LED10.anode, R10.Pin_0, R10.Pin_1
  N11: Componente1.D12/MISO, LED11.anode, R11.Pin_0, R11.Pin_1
  N12: Componente1.D13/SCK, LED12.anode, R12.Pin_0, R12.Pin_1
  GND: Componente1.GND, LED13.cathode, LED14.cathode, LED15.cathode, LED16.cathode, LED17.cathode, Componente4.GND
  N13: Componente1.D1/TX, LED13.anode, R17.Pin_0, R17.Pin_1
  N14: Componente1.D2, LED1.anode, R1.Pin_0, R1.Pin_1
  N15: Componente1.D3_PWM, LED2.anode, R2.Pin_0, R2.Pin_1
  N16: Componente1.D4, LED3.anode, R3.Pin_0, R3.Pin_1
  N17: Componente1.D5_PWM, LED4.anode, R4.Pin_0, R4.Pin_1
  N18: Componente1.D6_PWM, LED5.anode, R5.Pin_0, R5.Pin_1
  N19: Componente1.D7, LED6.anode, R6.Pin_0, R6.Pin_1
  5V: Componente1.5V, Componente4.VCC
  N20: LED1.cathode, LED2.cathode, LED3.cathode, LED4.cathode, LED5.cathode, LED6.cathode, LED7.cathode, LED8.cathode, LED9.cathode, LED10.cathode, LED11.cathode, LED12.cathode
