# Fritzing sketch relojs (saved by Fritzing 0.9.3b)
circuit board: 16.2911cm x 16cm
breadboards: 1

parts:
  LED1 = LED - 5mm [color="Red (633nm)" package="5 mm [THT]"]
  LED2 = LED - 5mm [color="Red (633nm)" package="5 mm [THT]"]
  LED3 = LED - 5mm [color="Red (633nm)" package="5 mm [THT]"]
  LED4 = LED - 5mm [color="Red (633nm)" package="5 mm [THT]"]
  LED5 = LED - 5mm [color="Red (633nm)" package="5 mm [THT]"]
  LED6 = LED - 5mm [color="Red (633nm)" package="5 mm [THT]"]
  LED7 = LED - 5mm [color="Red (633nm)" package="5 mm [THT]"]
  LED8 = LED - 5mm [color="Red (633nm)" package="5 mm [THT]"]
  LED9 = LED - 5mm [color="Red (633nm)" package="5 mm [THT]"]
  LED10 = LED - 5mm [color="Red (633nm)" package="5 mm [THT]"]
  LED11 = LED - 5mm [color="Red (633nm)" package="5 mm [THT]"]
  LED12 = LED - 5mm [color="Red (633nm)" package="5 mm [THT]"]
  Componente1 = Arduino Uno (Rev3)
  R1 = Resistor [tolerance=±5% resistance=1k package=THT]
  LED13 = LED - 5mm [color="Orange (620nm)" package="5 mm [THT]"]
  LED14 = LED - 5mm [color="Orange (620nm)" package="5 mm [THT]"]
  LED15 = LED - 5mm [color="Orange (620nm)" package="5 mm [THT]"]
  LED16 = LED - 5mm [color="Orange (620nm)" package="5 mm [THT]"]
  LED17 = LED - 5mm [color="Orange (620nm)" package="5 mm [THT]"]
  R2 = Resistor [tolerance=±5% resistance=1k package=THT]
  R3 = Resistor [tolerance=±5% resistance=1k package=THT]
  R4 = Resistor [tolerance=±5% resistance=1k package=THT]
  R5 = Resistor [tolerance=±5% resistance=1k package=THT]
  R6 = Resistor [tolerance=±5% resistance=1k package=THT]
  R7 = Resistor [tolerance=±5% resistance=1k package=THT]
  R8 = Resistor [tolerance=±5% resistance=1k package=THT]
  R9 = Resistor [tolerance=±5% resistance=1k package=THT]
  R10 = Resistor [tolerance=±5% resistance=1k package=THT]
  R11 = Resistor [tolerance=±5% resistance=1k package=THT]
  R12 = Resistor [tolerance=±5% resistance=1k package=THT]
  R13 = Resistor [tolerance=±5% resistance=1k package=THT]
  R14 = Resistor [tolerance=±5% resistance=1k package=THT]
  R15 = Resistor [tolerance=±5% resistance=1k package=THT]
  R16 = Resistor [tolerance=±5% resistance=1k package=THT]
  R17 = Resistor [tolerance=±5% resistance=1k package=THT]
  Componente2 = DeadOn RTC - DS3234 Breakout
  R18 = Resistor [tolerance=±5% resistance=1k package=THT]

nets:
  GND: LED1.cathode, LED2.cathode, LED3.cathode, LED4.cathode, LED5.cathode, LED6.cathode, LED7.cathode, LED8.cathode, LED9.cathode, LED10.cathode, LED11.cathode, LED12.cathode, Componente1.GND, LED13.cathode, LED14.cathode, LED15.cathode, LED16.cathode, LED17.cathode, Componente2.GND
  N1: LED1.anode, R1.Pin_0
  N2: LED2.anode, R2.Pin_0
  N3: LED3.anode, R3.Pin_0
  N4: LED4.anode, R4.Pin_0
  N5: LED5.anode, R5.Pin_0
  N6: LED6.anode, R6.Pin_0
  N7: LED7.anode, R7.Pin_0
  N8: LED8.anode, R8.Pin_0
  N9: LED9.anode, R9.Pin_0
  N10: LED10.anode, R10.Pin_0
  N11: LED11.anode, R11.Pin_0
  N12: LED12.anode, R12.Pin_0
  N13: Componente1.A0, R14.Pin_1
  N14: Componente1.A1, R15.Pin_1
  N15: Componente1.A2, R16.Pin_1
  N16: Componente1.A3, R17.Pin_1
  N17: Componente1.A4/SDA, Componente2.INT/SQW
  N18: Componente1.A5/SCL, Componente2.SCLK
  N19: Componente1.D8, R7.Pin_1
  N20: Componente1.D9_PWM, R8.Pin_1
  N21: Componente1.D10_PWM/SS, R9.Pin_1
  N22: Componente1.D11_PWM/MOSI, R10.Pin_1
  N23: Componente1.D12/MISO, R11.Pin_1
  N24: Componente1.D13/SCK, R12.Pin_1
  N25: Componente1.D1/TX, R13.Pin_1
  N26: Componente1.D2, R1.Pin_1
  N27: Componente1.D3_PWM, R2.Pin_1
  N28: Componente1.D4, R3.Pin_1
  N29: Componente1.D5_PWM, R4.Pin_1
  N30: Componente1.D6_PWM, R5.Pin_1
  N31: Componente1.D7, R6.Pin_1
  N32: Componente1.5V, R18.Pin_0
  N33: LED13.anode, R13.Pin_0
  N34: LED14.anode, R14.Pin_0
  N35: LED15.anode, R15.Pin_0
  N36: LED16.anode, R16.Pin_0
  N37: LED17.anode, R17.Pin_0
  N38: Componente2.VCC, R18.Pin_1
